// Logisim project Regfile.circ as structural Verilog: 1 circuit, main circuit main
module main (
  input  [1:0] Read_register_1,
  input  [1:0] Read_register_2,
  input  [1:0] write_register,
  input  [15:0] write_data,
  input  RegWrite,
  input  clock,
  output [15:0] Reg_0_Value,
  output [15:0] Reg_1_Value,
  output [15:0] Reg_2_Value,
  output [15:0] Reg_3_Value,
  output [15:0] Read_Data_1,
  output [15:0] Read_Data_2
);

  wire [15:0] multiplexer_1_out, multiplexer_2_out, multiplexer_3_out, multiplexer_4_out;

  Multiplexer #(.select(3), .width(16), .enable("false")) multiplexer_1 (
    .in0(Reg_0_Value), .in1(Reg_0_Value), .in2(Reg_0_Value), .in3(Reg_0_Value), .in4(write_data),
    .in5(Reg_0_Value), .in6(Reg_0_Value), .in7(Reg_0_Value), .out(multiplexer_1_out),
    .sel({RegWrite, write_register}));
  Register #(.width(16)) register_1 (.D(multiplexer_1_out), .en(1'b1), .Q(Reg_0_Value), .clk(clock), .clr(1'b0));
  Register #(.width(16)) register_2 (.D(multiplexer_2_out), .en(1'b1), .Q(Reg_1_Value), .clk(clock), .clr(1'b0));
  Multiplexer #(.select(3), .width(16), .enable("false")) multiplexer_2 (
    .in0(Reg_1_Value), .in1(Reg_1_Value), .in2(Reg_1_Value), .in3(Reg_1_Value), .in4(Reg_1_Value),
    .in5(write_data), .in6(Reg_1_Value), .in7(Reg_1_Value), .out(multiplexer_2_out),
    .sel({RegWrite, write_register}));
  Register #(.width(16)) register_3 (.D(multiplexer_3_out), .en(1'b1), .Q(Reg_2_Value), .clk(clock), .clr(1'b0));
  Multiplexer #(.select(3), .width(16), .enable("false")) multiplexer_3 (
    .in0(Reg_2_Value), .in1(Reg_2_Value), .in2(Reg_2_Value), .in3(Reg_2_Value), .in4(Reg_2_Value),
    .in5(Reg_2_Value), .in6(write_data), .in7(Reg_2_Value), .out(multiplexer_3_out),
    .sel({RegWrite, write_register}));
  Multiplexer #(.select(3), .width(16), .enable("false")) multiplexer_4 (
    .in0(Reg_3_Value), .in1(Reg_3_Value), .in2(Reg_3_Value), .in3(Reg_3_Value), .in4(Reg_3_Value),
    .in5(Reg_3_Value), .in6(Reg_3_Value), .in7(write_data), .out(multiplexer_4_out),
    .sel({RegWrite, write_register}));
  Register #(.width(16)) register_4 (.D(multiplexer_4_out), .en(1'b1), .Q(Reg_3_Value), .clk(clock), .clr(1'b0));
  Multiplexer #(.select(2), .width(16), .enable("false")) multiplexer_5 (
    .in0(Reg_0_Value), .in1(Reg_1_Value), .in2(Reg_2_Value), .in3(Reg_3_Value), .out(Read_Data_1),
    .sel(Read_register_1));
  Multiplexer #(.select(2), .width(16), .enable("false")) multiplexer_6 (
    .in0(Reg_0_Value), .in1(Reg_1_Value), .in2(Reg_2_Value), .in3(Reg_3_Value), .out(Read_Data_2),
    .sel(Read_register_2));

  // Notes on the sheet:
  //   These are INPUTS to the circuit
  //   These are INPUTS to the circuit
  //   DO NOT CHANGE THE LOCATIONS OF THE INPUTS/OUTPUTS! IF YOU DO SO, YOU NEED TO MAKE SURE THE PINS ARE AT THE RIGHT PLACE!
  //   These are OUTPUTS to the circuit
  //   Yet again, the clock is not an actual clock, but an input, one that will should/will be inputed from the higher circuit
  //   These are OUTPUTS to the circuit
endmodule
