// Logisim project alu.circ as structural Verilog: 7 circuits, main circuit main
module main (
  input  [15:0] X,
  input  [15:0] Y,
  input  [3:0] switch__S,
  output signed_overflow,
  output [15:0] result,
  output equal
);

  wire comparator_1_lt;
  wire [4:0] bitadder_1_out;
  wire [15:0] adder_1_out, and_1_out, bit_extender_1_out, bit_extender_2_out, ffo16_1_output, or_1_out,
       shifter_1_out, shifter_2_out, shifter_3_out, shifter_4_out, subtractor_1_out, zb_1_output;

  assign and_1_out = X & Y;  // AND_Gate and_1, 16 bits wide
  assign or_1_out = X | Y;  // OR_Gate or_1, 16 bits wide
  Comparator #(.width(16)) comparator_1 (.a(X), .b(Y), .eq(equal), .lt(comparator_1_lt));  // open: gt
  Shifter #(.width(16)) shifter_1 (.in(X), .\dist (Y[3:0]), .out(shifter_1_out));
  Shifter #(.width(16), .shift("lr")) shifter_2 (.in(X), .\dist (Y[3:0]), .out(shifter_2_out));
  Shifter #(.width(16), .shift("ar")) shifter_3 (.in(X), .\dist (Y[3:0]), .out(shifter_3_out));
  Adder #(.width(16)) adder_1 (.a(X), .b(Y), .out(adder_1_out));  // open: cin, cout
  Subtractor #(.width(16)) subtractor_1 (.a(X), .b(Y), .out(subtractor_1_out));  // open: bin, bout
  ffo16 ffo16_1 (.R_rs(X), .\output (ffo16_1_output));
  zb zb_1 (.R_rs(X), .\output (zb_1_output));
  assign bit_extender_1_out = {{11{1'b0}}, bitadder_1_out};  // Bit_Extender bit_extender_1
  BitAdder #(.width(16)) bitadder_1 (.in0(X), .out(bitadder_1_out));
  Shifter #(.width(16)) shifter_4 (.in(Y), .\dist (4'b1000), .out(shifter_4_out));
  assign bit_extender_2_out = {{15{1'b0}}, comparator_1_lt};  // Bit_Extender bit_extender_2
  signedOverflow signedoverflow_1 (
    .inp1(X), .inp2(Y), .sum(adder_1_out), .difference(subtractor_1_out), .out(signed_overflow));
  Multiplexer #(.select(4), .width(16), .enable("false")) multiplexer_1 (
    .in0(and_1_out), .in1(or_1_out), .in2(bit_extender_2_out), .in3(shifter_1_out), .in4(shifter_2_out),
    .in5(shifter_3_out), .in6(adder_1_out), .in7(subtractor_1_out), .in8(ffo16_1_output), .in9(zb_1_output),
    .in10(bit_extender_1_out), .in11(shifter_4_out), .out(result), .sel(switch__S));  // open: in12, in13, in14, in15

  // Notes on the sheet:
  //   These are INPUTS to your circuit
  //   This is an INPUT to your circuit
  //   DO NOT CHANGE THE LOCATIONS OF THE INPUTS/OUTPUTS! IF YOU DO SO, YOU NEED TO MAKE SURE THE PINS ARE AT THE RIGHT PLACE!
  //   These are OUTPUTS to your circuit
endmodule

module ffo16 (
  input  [15:0] R_rs,
  output [15:0] \output 
);

  wire comparator_1_eq, comparator_2_eq;
  wire [15:0] adder_1_out, ffo8_1_output, ffo8_2_output, multiplexer_1_out;

  ffo8 ffo8_1 (.\input (R_rs[15:8]), .\output (ffo8_1_output));
  ffo8 ffo8_2 (.\input (R_rs[7:0]), .\output (ffo8_2_output));
  // Probe on ffo8_1_output
  Adder #(.width(16)) adder_1 (.a(ffo8_2_output), .b(16'h8), .out(adder_1_out));  // open: cin, cout
  Comparator comparator_1 (.a(R_rs[15:8]), .b({8{1'b0}}), .eq(comparator_1_eq));  // open: gt, lt
  Comparator #(.width(16)) comparator_2 (.a(R_rs), .b({16{1'b0}}), .eq(comparator_2_eq));  // open: gt, lt
  Multiplexer #(.width(16), .enable("false")) multiplexer_1 (
    .in0(ffo8_1_output), .in1(adder_1_out), .out(multiplexer_1_out), .sel(comparator_1_eq));
  Multiplexer #(.width(16), .enable("false")) multiplexer_2 (
    .in0(multiplexer_1_out), .in1(16'h10), .out(\output ), .sel(comparator_2_eq));
endmodule

module ffo8 (
  input  [7:0] \input ,
  output [15:0] \output 
);

  wire comparator_1_eq, comparator_2_eq;
  wire [15:0] adder_1_out, ffo4_1_output, ffo4_2_output, multiplexer_1_out;

  ffo4 ffo4_1 (.\input (\input [7:4]), .\output (ffo4_1_output));
  ffo4 ffo4_2 (.\input (\input [3:0]), .\output (ffo4_2_output));
  Adder #(.width(16)) adder_1 (.a(ffo4_2_output), .b(16'h4), .out(adder_1_out));  // open: cin, cout
  Comparator #(.width(4)) comparator_1 (.a(\input [7:4]), .b(4'b0000), .eq(comparator_1_eq));  // open: gt, lt
  Comparator comparator_2 (.a(\input ), .b({8{1'b0}}), .eq(comparator_2_eq));  // open: gt, lt
  Multiplexer #(.width(16), .enable("false")) multiplexer_1 (
    .in0(ffo4_1_output), .in1(adder_1_out), .out(multiplexer_1_out), .sel(comparator_1_eq));
  Multiplexer #(.width(16), .enable("false")) multiplexer_2 (
    .in0(multiplexer_1_out), .in1(16'h8), .out(\output ), .sel(comparator_2_eq));
endmodule

module ffo4 (
  input  [3:0] \input ,
  output [15:0] \output 
);

  wire comparator_1_eq, comparator_2_eq;
  wire [15:0] adder_1_out, ffo2_1_output, ffo2_2_output, multiplexer_1_out;

  ffo2 ffo2_1 (.\input (\input [3:2]), .\output (ffo2_1_output));
  ffo2 ffo2_2 (.\input (\input [1:0]), .\output (ffo2_2_output));
  Comparator #(.width(2)) comparator_1 (.a(\input [3:2]), .b(2'b00), .eq(comparator_1_eq));  // open: gt, lt
  Adder #(.width(16)) adder_1 (.a(ffo2_2_output), .b(16'h2), .out(adder_1_out));  // open: cin, cout
  Comparator #(.width(4)) comparator_2 (.a(\input ), .b(4'b0000), .eq(comparator_2_eq));  // open: gt, lt
  Multiplexer #(.width(16), .enable("false")) multiplexer_1 (
    .in0(ffo2_1_output), .in1(adder_1_out), .out(multiplexer_1_out), .sel(comparator_1_eq));
  Multiplexer #(.width(16), .enable("false")) multiplexer_2 (
    .in0(multiplexer_1_out), .in1(16'h4), .out(\output ), .sel(comparator_2_eq));
endmodule

module ffo2 (
  input  [1:0] \input ,
  output [15:0] \output 
);

  wire comparator_1_eq, comparator_2_eq;
  wire [15:0] multiplexer_1_out;

  Comparator #(.width(1)) comparator_1 (.a(\input [1]), .b(1'b0), .eq(comparator_1_eq));  // open: gt, lt
  Comparator #(.width(2)) comparator_2 (.a(\input ), .b(2'b00), .eq(comparator_2_eq));  // open: gt, lt
  Multiplexer #(.width(16), .enable("false")) multiplexer_1 (
    .in0({16{1'b0}}), .in1(16'h1), .out(multiplexer_1_out), .sel(comparator_1_eq));
  Multiplexer #(.width(16), .enable("false")) multiplexer_2 (
    .in0(multiplexer_1_out), .in1(16'h2), .out(\output ), .sel(comparator_2_eq));
endmodule

module zb (
  input  [15:0] R_rs,
  output [15:0] \output 
);

  wire comparator_1_eq, comparator_2_eq, comparator_3_eq, comparator_4_eq, comparator_5_eq, comparator_6_eq,
       comparator_7_eq, comparator_8_eq, comparator_9_eq, or_1_out;

  Comparator comparator_1 (.a({8{1'b0}}), .b(R_rs[7:0]), .eq(comparator_1_eq));  // open: gt, lt
  Comparator comparator_2 (.a({8{1'b0}}), .b(R_rs[8:1]), .eq(comparator_2_eq));  // open: gt, lt
  Comparator comparator_3 (.b(R_rs[9:2]), .eq(comparator_3_eq));  // open: a, gt, lt
  Comparator comparator_4 (.b(R_rs[10:3]), .eq(comparator_4_eq));  // open: a, gt, lt
  Comparator comparator_5 (.b(R_rs[11:4]), .eq(comparator_5_eq));  // open: a, gt, lt
  Comparator comparator_6 (.b(R_rs[12:5]), .eq(comparator_6_eq));  // open: a, gt, lt
  Comparator comparator_7 (.b(R_rs[13:6]), .eq(comparator_7_eq));  // open: a, gt, lt
  Comparator comparator_8 (.b(R_rs[14:7]), .eq(comparator_8_eq));  // open: a, gt, lt
  Comparator comparator_9 (.a({8{1'b0}}), .b(R_rs[15:8]), .eq(comparator_9_eq));  // open: gt, lt
  or or_1 (or_1_out, comparator_1_eq, comparator_2_eq, comparator_3_eq, comparator_4_eq, comparator_5_eq, comparator_6_eq, comparator_7_eq, comparator_8_eq, comparator_9_eq);
  Multiplexer #(.width(16), .enable("false")) multiplexer_1 (
    .in0({16{1'b0}}), .in1(16'h1), .out(\output ), .sel(or_1_out));
endmodule

module signedOverflow (
  input  [15:0] inp1,
  input  [15:0] inp2,
  input  [15:0] sum,
  input  [15:0] difference,
  output out
);

  wire and_1_out, and_2_out, and_3_out, and_4_out;

  and and_1 (and_1_out, ~inp1[15], ~inp2[15], sum[15]);  // AND_Gate
  and and_2 (and_2_out, inp1[15], inp2[15], ~inp2[15]);  // AND_Gate
  and and_3 (and_3_out, inp1[15], ~inp2[15], ~difference[15]);  // AND_Gate
  and and_4 (and_4_out, ~inp1[15], inp2[15], difference[15]);  // AND_Gate
  or or_1 (out, and_1_out, and_2_out, and_3_out, and_4_out);
endmodule
