// Logisim project cpu.circ as structural Verilog: 2 circuits, main circuit main
// aluOut
module main (
  input  [15:0] From_Instr_Mem,
  input  clk,
  output [15:0] r0,
  output [15:0] r1,
  output [15:0] r2,
  output [15:0] r3,
  output [15:0] Display_0,
  output [15:0] Display_1,
  output [15:0] To_Instr_Mem,
  output [15:0] Data_Mem_Data,
  output [15:0] Data_Mem_Addr,
  output Data_Mem_Write
);

  wire aluEqual, aluSource, comparator_1_eq, comparator_2_eq, comparator_3_eq, comparator_4_eq, display,
       memToReg, multiplexer_8_out, multiplexer_9_out, not_1_out, not_2_out, not_3_out, not_4_out, overflow,
       regWrite, Reset_out, signExtend;
  wire [1:0] addrType, destSource, multiplexer_4_out;
  wire [3:0] aluFunc, func, op;
  wire [7:4] imm;
  wire [11:8] jAddr;
  wire [15:0] adder_1_out, bit_extender_1_out, bit_extender_2_out, extendedImm, multiplexer_2_out,
       multiplexer_3_out, multiplexer_5_out, multiplexer_6_out, nextPC, pcPlus1, R_rs, R_rt;

  Adder #(.width(16)) adder_1 (.a(To_Instr_Mem), .b(extendedImm), .out(adder_1_out));  // open: cin, cout
  Register #(.width(16)) PC (.D(nextPC), .en(1'b1), .Q(To_Instr_Mem), .clk(clk), .clr(1'b0));
  Adder #(.width(16)) adder_2 (.a(To_Instr_Mem), .b(16'h1), .out(pcPlus1));  // open: cin, cout
  Comparator #(.width(2)) comparator_1 (.a(addrType), .b(2'b00), .eq(comparator_1_eq));  // open: gt, lt
  Comparator #(.width(2)) comparator_2 (.a(destSource), .b(2'b10), .eq(comparator_2_eq));  // open: gt, lt
  Multiplexer #(.select(2), .width(16), .enable("false")) multiplexer_1 (
    .in0(pcPlus1), .in1({To_Instr_Mem[15:12], jAddr, imm, func}), .in2(adder_1_out), .in3(R_rs),
    .out(nextPC), .sel(addrType));
  not not_1 (not_1_out, comparator_1_eq);
  not not_2 (not_2_out, comparator_2_eq);
  Multiplexer #(.width(16), .enable("false")) multiplexer_2 (
    .in0(To_Instr_Mem), .in1(multiplexer_5_out), .out(multiplexer_2_out), .sel(not_2_out));
  Multiplexer #(.width(16), .enable("false")) multiplexer_3 (
    .in0(From_Instr_Mem), .in1({16{1'b0}}), .out(multiplexer_3_out), .sel(not_1_out));
  Register #(.width(16)) register_1 (
    .D(multiplexer_3_out), .Q({op, jAddr, imm, func}), .clk(clk), .clr(1'b0));  // open: en
  Multiplexer #(.select(2), .width(2), .enable("false")) multiplexer_4 (
    .in0(jAddr[9:8]), .in1(imm[7:6]), .in2(2'b11), .out(multiplexer_4_out), .sel(destSource));  // open: in3
  Regfile_main main_1 (
    .Read_register_1(jAddr[11:10]), .Read_register_2(jAddr[9:8]), .write_register(multiplexer_4_out),
    .write_data(multiplexer_2_out), .Reg_0_Value(r0), .Reg_1_Value(r1), .Reg_2_Value(r2), .Reg_3_Value(r3),
    .RegWrite(regWrite), .clock(clk), .Read_Data_1(R_rs), .Read_Data_2(R_rt));
  assign bit_extender_1_out = {{8{1'b0}}, {imm, func}};  // Bit_Extender bit_extender_1
  assign bit_extender_2_out = {{8{imm[7]}}, {imm, func}};  // Bit_Extender bit_extender_2
  Multiplexer #(.width(16), .enable("false")) multiplexer_5 (
    .in0(Data_Mem_Data), .in1(Data_Mem_Addr), .out(multiplexer_5_out), .sel(not_3_out));
  not not_3 (not_3_out, memToReg);
  alu_main main_2 (
    .switch__S(aluFunc), .X(R_rs), .equal(aluEqual), .result(Data_Mem_Addr), .signed_overflow(overflow),
    .Y(multiplexer_6_out));
  Multiplexer #(.width(16), .enable("false")) multiplexer_6 (
    .in0(extendedImm), .in1(R_rt), .out(multiplexer_6_out), .sel(aluSource));
  Multiplexer #(.width(16), .enable("false")) multiplexer_7 (
    .in0(bit_extender_1_out), .in1(bit_extender_2_out), .out(extendedImm), .sel(signExtend));
  control control_1 (
    .aluEqual(aluEqual), .op(op), .func(func), .addrType(addrType), .regWrite(regWrite),
    .signExtend(signExtend), .destSource(destSource), .aluFunc(aluFunc), .aluSource(aluSource),
    .memToReg(memToReg), .memWrite(Data_Mem_Write), .display(display));
  RAM #(.addrWidth(16), .dataWidth(16)) ram_1 (
    .addr(Data_Mem_Addr), .data(Data_Mem_Data), .sel(1'b1), .clk(clk), .ld(not_4_out), .clr(Reset_out));
  not not_4 (not_4_out, Data_Mem_Write);
  Button Reset (.out(Reset_out));
  Multiplexer #(.enable("false")) multiplexer_8 (
    .in0(display), .in1(1'b0), .out(multiplexer_8_out), .sel(comparator_3_eq));
  Comparator comparator_3 (.a(8'h1), .b({imm, func}), .eq(comparator_3_eq));  // open: gt, lt
  Multiplexer #(.enable("false")) multiplexer_9 (
    .in0(display), .in1(1'b0), .out(multiplexer_9_out), .sel(comparator_4_eq));
  Comparator comparator_4 (.a({8{1'b0}}), .b({imm, func}), .eq(comparator_4_eq));  // open: gt, lt
  assign Data_Mem_Data = Data_Mem_Write ? R_rt : 16'bz;  // Controlled_Buffer controlled_buffer_1
  Register #(.width(16)) register_2 (.D(R_rs), .en(multiplexer_8_out), .Q(Display_0), .clk(clk), .clr(1'b0));
  Register #(.width(16)) register_3 (.D(R_rs), .en(multiplexer_9_out), .Q(Display_1), .clk(clk), .clr(1'b0));
  Hex_Digit_Display hex_digit_display_1 (.value(Display_0[15:12]));  // open: dp
  Hex_Digit_Display hex_digit_display_2 (.value(Display_0[11:8]));  // open: dp
  Hex_Digit_Display hex_digit_display_3 (.value(Display_1[15:12]));  // open: dp
  Hex_Digit_Display hex_digit_display_4 (.value(Display_1[11:8]));  // open: dp
  LED u_overflow (.in(overflow));
  Hex_Digit_Display hex_digit_display_5 (.value(Display_0[7:4]));  // open: dp
  Hex_Digit_Display hex_digit_display_6 (.value(Display_0[3:0]));  // open: dp
  Hex_Digit_Display hex_digit_display_7 (.value(Display_1[7:4]));  // open: dp
  Hex_Digit_Display hex_digit_display_8 (.value(Display_1[3:0]));  // open: dp

  // Other names for the same wires on the sheet: aluOut[15:0] = Data_Mem_Addr; d0[15:0] = Display_0;
  //   d1[15:0] = Display_1; imm[3:0] = func; jAddr (some bits) = {To_Instr_Mem[15:12], imm, func}; rd[1:0] = imm[7:6];
  //   rt[1:0] = jAddr[9:8]; rs[1:0] = jAddr[11:10]; PC[15:0] = To_Instr_Mem; memOut[15:0] = Data_Mem_Data;
  //   memWrite = Data_Mem_Write

  // Notes on the sheet:
  //   The instruction that you would receive as INPUT
  //   This is the current PC that you need to send as OUTPUT
  //   This is a CLK that is an INPUT driven from the harness.
  //   Remember, this circuit is loaded from the harness to be tested!
  //   DO NOT CHANGE THE LOCATIONS OF THE INPUTS/OUTPUTS! IF YOU DO SO, YOU NEED TO MAKE SURE THE PINS ARE AT THE RIGHT PLACE!
  //   These are OUTPUTS to the circuit
  //   These are OUTPUTS to the circuit
endmodule

module control (
  input  aluEqual,
  input  [3:0] op,
  input  [3:0] func,
  output [1:0] addrType,
  output regWrite,
  output signExtend,
  output [1:0] destSource,
  output aluSource,
  output memToReg,
  output memWrite,
  output display,
  output [3:0] aluFunc
);

  wire [1:0] multiplexer_1_out, multiplexer_2_out;

  Multiplexer #(.width(2), .enable("false")) multiplexer_1 (
    .in0(2'b00), .in1(2'b10), .out(multiplexer_1_out), .sel(aluEqual));
  Multiplexer #(.width(2), .enable("false")) multiplexer_2 (
    .in0(2'b10), .in1(2'b00), .out(multiplexer_2_out), .sel(aluEqual));
  Multiplexer #(.select(4), .enable("false")) multiplexer_3 (
    .in0(1'b1), .in1(1'b1), .in2(1'b1), .in3(1'b1), .in4(1'b1), .in5(1'b1), .in6(1'b1), .in7(1'b1),
    .in8(1'b0), .in9(1'b0), .in10(1'b0), .in11(1'b0), .in12(1'b0), .in13(1'b1), .in14(1'b1), .in15(1'b0),
    .out(regWrite), .sel(op));
  Multiplexer #(.select(4), .width(2), .enable("false")) multiplexer_4 (
    .in0(2'b00), .in1(2'b00), .in2(2'b00), .in3(2'b00), .in4(2'b00), .in5(2'b00), .in6(2'b00), .in7(2'b01),
    .in8(2'b01), .in9(2'b11), .in10(multiplexer_1_out), .in11(multiplexer_2_out), .in12(2'b00), .in13(2'b00),
    .in14(2'b00), .in15(2'b00), .out(addrType), .sel(op));
  Multiplexer #(.select(4), .enable("false")) multiplexer_5 (
    .in1(1'b0), .in2(1'b0), .in3(1'b0), .in4(1'b1), .in5(1'b0), .in6(1'b0), .in10(1'b1), .in11(1'b1),
    .in12(1'b1), .in13(1'b0), .in14(1'b1), .in15(1'b0), .out(signExtend), .sel(op));  // open: in0, in7, in8, in9
  Multiplexer #(.select(4), .width(2), .enable("false")) multiplexer_6 (
    .in0(2'b01), .in1(2'b00), .in2(2'b00), .in3(2'b00), .in4(2'b00), .in5(2'b00), .in6(2'b00), .in7(2'b10),
    .in13(2'b00), .in14(2'b00), .out(destSource), .sel(op));  // open: in8, in9, in10, in11, in12, in15
  Multiplexer #(.select(4), .width(4), .enable("false")) multiplexer_7 (
    .in0(func), .in1(4'b1000), .in2(4'b1001), .in3(4'b1010), .in4(4'b0110), .in5(4'b0000), .in6(4'b0001),
    .in12(4'b0110), .in13(4'b1011), .in14(4'b0110), .out(aluFunc), .sel(op));  // open: in7, in8, in9, in10, in11, in15
  Multiplexer #(.select(4), .enable("false")) multiplexer_8 (
    .in0(1'b1), .in1(1'b0), .in2(1'b0), .in3(1'b0), .in4(1'b0), .in5(1'b0), .in6(1'b0), .in10(1'b1),
    .in11(1'b1), .in12(1'b0), .in13(1'b0), .in14(1'b0), .in15(1'b0), .out(aluSource), .sel(op));  // open: in7, in8, in9
  Multiplexer #(.select(4), .enable("false")) multiplexer_9 (
    .in0(1'b0), .in1(1'b0), .in2(1'b0), .in3(1'b0), .in4(1'b0), .in5(1'b0), .in6(1'b0), .in7(1'b0),
    .in8(1'b0), .in9(1'b0), .in10(1'b0), .in11(1'b0), .in12(1'b0), .in13(1'b0), .in14(1'b1), .in15(1'b0),
    .out(memToReg), .sel(op));
  Multiplexer #(.select(4), .enable("false")) multiplexer_10 (
    .in0(1'b0), .in1(1'b0), .in2(1'b0), .in3(1'b0), .in4(1'b0), .in5(1'b0), .in6(1'b0), .in7(1'b0),
    .in8(1'b0), .in9(1'b0), .in10(1'b0), .in11(1'b0), .in12(1'b1), .in13(1'b0), .in14(1'b0), .in15(1'b0),
    .out(memWrite), .sel(op));
  Multiplexer #(.select(4), .enable("false")) multiplexer_11 (
    .in0(1'b0), .in1(1'b0), .in2(1'b0), .in3(1'b0), .in4(1'b0), .in5(1'b0), .in6(1'b0), .in7(1'b0),
    .in8(1'b0), .in9(1'b0), .in10(1'b0), .in11(1'b0), .in12(1'b0), .in13(1'b0), .in14(1'b0), .in15(1'b1),
    .out(display), .sel(op));
endmodule
